// Logisim project logism-img-32x32.circ as structural Verilog: 3 circuits, main circuit main
module main (
);

  wire clock, Column_1, Column_2, Column_3, Column_4, Column_5, Column_6, Column_7, Column_8, Column_9,
       Column_10, Column_11, Column_12, Column_13, Column_14, Column_15, Column_16, Column_17, Column_18,
       Column_19, Column_20, Column_21, Column_22, Column_23, Column_24, Column_25, Column_26, Column_27,
       Column_28, Column_29, Column_30, Column_31, Column_32;
  wire [4:0] bitselector_1_out;
  wire [11:0] counter_1_q;
  wire [31:0] Column_1_Data, Column_2_Data, Column_3_Data, Column_4_Data, Column_5_Data, Column_6_Data,
       Column_7_Data, Column_8_Data, Column_9_Data, Column_10_Data, Column_11_Data, Column_12_Data,
       Column_13_Data, Column_14_Data, Column_15_Data, Column_16_Data, Column_17_Data, Column_18_Data,
       Column_19_Data, Column_20_Data, Column_21_Data, Column_22_Data, Column_23_Data, Column_24_Data,
       Column_25_Data, Column_26_Data, Column_27_Data, Column_28_Data, Column_29_Data, Column_30_Data,
       Column_31_Data, Column_32_Data, data;

  Counter #(.width(12), .max('hfff)) counter_1 (.Q(counter_1_q), .clk(clock));  // open: load, D, count, carry, clr
  Clock clock_1 (.out(clock));
  RAM #(.addrWidth(12), .dataWidth(32)) ram_1 (.addr(counter_1_q), .data(data));  // open: sel, clk, ld, clr
  Demultiplexer #(.select(5)) demultiplexer_1 (
    .out0(Column_1), .out1(Column_2), .out2(Column_3), .out3(Column_4), .out4(Column_5), .out5(Column_6),
    .out6(Column_7), .out7(Column_8), .out8(Column_9), .out9(Column_10), .out10(Column_11),
    .out11(Column_12), .out12(Column_13), .out13(Column_14), .out14(Column_15), .out15(Column_16),
    .out16(Column_17), .out17(Column_18), .out18(Column_19), .out19(Column_20), .out20(Column_21),
    .out21(Column_22), .out22(Column_23), .out23(Column_24), .out24(Column_25), .out25(Column_26),
    .out26(Column_27), .out27(Column_28), .out28(Column_29), .out29(Column_30), .out30(Column_31),
    .out31(Column_32), .in(1'b1), .sel(bitselector_1_out));  // open: en
  BitSelector #(.width(12), .group(5)) bitselector_1 (.in(counter_1_q), .out(bitselector_1_out), .sel(2'b00));
  Data_Registers_32 data_registers_32_1 (
    .Col_1_Data(Column_1_Data), .Col_2_Data(Column_2_Data), .Col_3_Data(Column_3_Data),
    .Col_4_Data(Column_4_Data), .Col_5_Data(Column_5_Data), .Col_6_Data(Column_6_Data),
    .Col_7_Data(Column_7_Data), .Col_8_Data(Column_8_Data), .Col_9_Data(Column_9_Data),
    .Col_10_Data(Column_10_Data), .Col_11_Data(Column_11_Data), .Col_12_Data(Column_12_Data),
    .Col_13_Data(Column_13_Data), .Col_14_Data(Column_14_Data), .Col_15_Data(Column_15_Data),
    .Col_16_Data(Column_16_Data), .Col_17_Data(Column_17_Data), .Col_18_Data(Column_18_Data),
    .Col_19_Data(Column_19_Data), .Col_20_Data(Column_20_Data), .Col_21_Data(Column_21_Data),
    .Col_22_Data(Column_22_Data), .Col_23_Data(Column_23_Data), .Col_24_Data(Column_24_Data),
    .Col_25_Data(Column_25_Data), .Col_26_Data(Column_26_Data), .Col_27_Data(Column_27_Data),
    .Col_28_Data(Column_28_Data), .Col_29_Data(Column_29_Data), .Col_30_Data(Column_30_Data),
    .Col_31_Data(Column_31_Data), .Col_32_Data(Column_32_Data), .Data_Input(data), .Col_1_Input(Column_1),
    .Col_2_Input(Column_2), .Col_3_Input(Column_3), .Col_4_Input(Column_4), .Col_5_Input(Column_5),
    .Col_6_Input(Column_6), .Col_7_Input(Column_7), .Col_8_Input(Column_8), .Col_9_Input(Column_9),
    .Col_10_Input(Column_10), .Col_11_Input(Column_11), .Col_12_Input(Column_12), .Col_13_Input(Column_13),
    .Col_14_Input(Column_14), .Col_15_Input(Column_15), .Col_16_Input(Column_16), .Col_17_Input(Column_17),
    .Col_18_Input(Column_18), .Col_19_Input(Column_19), .Col_20_Input(Column_20), .Col_21_Input(Column_21),
    .Col_22_Input(Column_22), .Col_23_Input(Column_23), .Col_24_Input(Column_24), .Col_25_Input(Column_25),
    .Col_26_Input(Column_26), .Col_27_Input(Column_27), .Col_28_Input(Column_28), .Col_29_Input(Column_29),
    .Col_30_Input(Column_30), .Col_31_Input(Column_31), .Col_32_Input(Column_32));
  DotMatrix #(.matrixcols(32), .matrixrows(32)) dotmatrix_1 (
    .col0(Column_1_Data), .col1(Column_2_Data), .col2(Column_3_Data), .col3(Column_4_Data),
    .col4(Column_5_Data), .col5(Column_6_Data), .col6(Column_7_Data), .col7(Column_8_Data),
    .col8(Column_9_Data), .col9(Column_10_Data), .col10(Column_11_Data), .col11(Column_12_Data),
    .col12(Column_13_Data), .col13(Column_14_Data), .col14(Column_15_Data), .col15(Column_16_Data),
    .col16(Column_17_Data), .col17(Column_18_Data), .col18(Column_19_Data), .col19(Column_20_Data),
    .col20(Column_21_Data), .col21(Column_22_Data), .col22(Column_23_Data), .col23(Column_24_Data),
    .col24(Column_25_Data), .col25(Column_26_Data), .col26(Column_27_Data), .col27(Column_28_Data),
    .col28(Column_29_Data), .col29(Column_30_Data), .col30(Column_31_Data), .col31(Column_32_Data));

  // Notes on the sheet:
  //   Data RAM
endmodule

module Data_Registers_4 (
  input  Column_1_Input,
  input  Column_2_Input,
  input  Column_3_Input,
  input  Column_4_Input,
  input  [31:0] Data,
  output [31:0] out_6,
  output [31:0] out_7,
  output [31:0] out_8,
  output [31:0] out_9
);

  Register #(.width(32), .trigger("high")) register_1 (.D(Data), .Q(out_6), .clk(Column_1_Input));  // open: en, clr
  Register #(.width(32), .trigger("high")) register_2 (.D(Data), .Q(out_7), .clk(Column_2_Input));  // open: en, clr
  Register #(.width(32), .trigger("high")) register_3 (.D(Data), .Q(out_8), .clk(Column_3_Input));  // open: en, clr
  Register #(.width(32), .trigger("high")) register_4 (.D(Data), .Q(out_9), .clk(Column_4_Input));  // open: en, clr

  // Other names for the same wires on the sheet: Column_1 = Column_1_Input; Column_1_Data[31:0] = out_6;
  //   Column_2 = Column_2_Input; Column_2_Data[31:0] = out_7; Column_3 = Column_3_Input; Column_3_Data[31:0] = out_8;
  //   Column_4 = Column_4_Input; Column_4_Data[31:0] = out_9
endmodule

module Data_Registers_32 (
  input  Col_1_Input,
  input  Col_2_Input,
  input  Col_3_Input,
  input  Col_4_Input,
  input  Col_5_Input,
  input  Col_6_Input,
  input  Col_7_Input,
  input  Col_8_Input,
  input  Col_9_Input,
  input  Col_10_Input,
  input  Col_11_Input,
  input  Col_12_Input,
  input  Col_13_Input,
  input  Col_14_Input,
  input  Col_15_Input,
  input  Col_16_Input,
  input  Col_17_Input,
  input  Col_18_Input,
  input  Col_19_Input,
  input  Col_20_Input,
  input  Col_21_Input,
  input  Col_22_Input,
  input  Col_23_Input,
  input  Col_24_Input,
  input  Col_25_Input,
  input  Col_26_Input,
  input  Col_27_Input,
  input  Col_28_Input,
  input  Col_29_Input,
  input  Col_30_Input,
  input  [31:0] Data_Input,
  input  Col_31_Input,
  input  Col_32_Input,
  output [31:0] Col_1_Data,
  output [31:0] Col_2_Data,
  output [31:0] Col_3_Data,
  output [31:0] Col_4_Data,
  output [31:0] Col_5_Data,
  output [31:0] Col_6_Data,
  output [31:0] Col_7_Data,
  output [31:0] Col_8_Data,
  output [31:0] Col_9_Data,
  output [31:0] Col_10_Data,
  output [31:0] Col_11_Data,
  output [31:0] Col_12_Data,
  output [31:0] Col_13_Data,
  output [31:0] Col_14_Data,
  output [31:0] Col_15_Data,
  output [31:0] Col_16_Data,
  output [31:0] Col_17_Data,
  output [31:0] Col_18_Data,
  output [31:0] Col_19_Data,
  output [31:0] Col_20_Data,
  output [31:0] Col_21_Data,
  output [31:0] Col_22_Data,
  output [31:0] Col_23_Data,
  output [31:0] Col_24_Data,
  output [31:0] Col_25_Data,
  output [31:0] Col_26_Data,
  output [31:0] Col_27_Data,
  output [31:0] Col_28_Data,
  output [31:0] Col_29_Data,
  output [31:0] Col_30_Data,
  output [31:0] Col_31_Data,
  output [31:0] Col_32_Data
);

  Data_Registers_4 _1_4 (
    .out_6(Col_1_Data), .out_7(Col_2_Data), .out_8(Col_3_Data), .out_9(Col_4_Data), .Data(Data_Input),
    .Column_1_Input(Col_1_Input), .Column_2_Input(Col_2_Input), .Column_3_Input(Col_3_Input),
    .Column_4_Input(Col_4_Input));
  Data_Registers_4 _1_4_2 (
    .out_6(Col_9_Data), .out_7(Col_10_Data), .out_8(Col_11_Data), .out_9(Col_12_Data), .Data(Data_Input),
    .Column_1_Input(Col_9_Input), .Column_2_Input(Col_10_Input), .Column_3_Input(Col_11_Input),
    .Column_4_Input(Col_12_Input));
  Data_Registers_4 _1_4_3 (
    .out_6(Col_17_Data), .out_7(Col_18_Data), .out_8(Col_19_Data), .out_9(Col_20_Data), .Data(Data_Input),
    .Column_1_Input(Col_17_Input), .Column_2_Input(Col_18_Input), .Column_3_Input(Col_19_Input),
    .Column_4_Input(Col_20_Input));
  Data_Registers_4 _1_4_4 (
    .out_6(Col_25_Data), .out_7(Col_26_Data), .out_8(Col_27_Data), .out_9(Col_28_Data), .Data(Data_Input),
    .Column_1_Input(Col_25_Input), .Column_2_Input(Col_26_Input), .Column_3_Input(Col_27_Input),
    .Column_4_Input(Col_28_Input));
  Data_Registers_4 _5_8 (
    .out_6(Col_5_Data), .out_7(Col_6_Data), .out_8(Col_7_Data), .out_9(Col_8_Data), .Data(Data_Input),
    .Column_1_Input(Col_5_Input), .Column_2_Input(Col_6_Input), .Column_3_Input(Col_7_Input),
    .Column_4_Input(Col_8_Input));
  Data_Registers_4 _1_4_5 (
    .out_6(Col_13_Data), .out_7(Col_14_Data), .out_8(Col_15_Data), .out_9(Col_16_Data), .Data(Data_Input),
    .Column_1_Input(Col_13_Input), .Column_2_Input(Col_14_Input), .Column_3_Input(Col_15_Input),
    .Column_4_Input(Col_16_Input));
  Data_Registers_4 _1_4_6 (
    .out_6(Col_21_Data), .out_7(Col_22_Data), .out_8(Col_23_Data), .out_9(Col_24_Data), .Data(Data_Input),
    .Column_1_Input(Col_21_Input), .Column_2_Input(Col_22_Input), .Column_3_Input(Col_23_Input),
    .Column_4_Input(Col_24_Input));
  Data_Registers_4 _1_4_7 (
    .out_6(Col_29_Data), .out_7(Col_30_Data), .out_8(Col_31_Data), .out_9(Col_32_Data), .Data(Data_Input),
    .Column_1_Input(Col_29_Input), .Column_2_Input(Col_30_Input), .Column_3_Input(Col_31_Input),
    .Column_4_Input(Col_32_Input));

  // Other names for the same wires on the sheet: Column_1 = Col_1_Input; Column_1_Data[31:0] = Col_1_Data;
  //   Column_2 = Col_2_Input; Column_2_Data[31:0] = Col_2_Data; Column_3 = Col_3_Input;
  //   Column_3_Data[31:0] = Col_3_Data; Column_4 = Col_4_Input; Column_4_Data[31:0] = Col_4_Data;
  //   Column_5 = Col_5_Input; Column_5_Data[31:0] = Col_5_Data; Column_6 = Col_6_Input;
  //   Column_6_Data[31:0] = Col_6_Data; Column_7 = Col_7_Input; Column_7_Data[31:0] = Col_7_Data;
  //   Column_8 = Col_8_Input; Column_8_Data[31:0] = Col_8_Data; Column_9 = Col_9_Input;
  //   Column_9_Data[31:0] = Col_9_Data; Column_10 = Col_10_Input; Column_10_Data[31:0] = Col_10_Data;
  //   Column_11 = Col_11_Input; Column_11_Data[31:0] = Col_11_Data; Column_12 = Col_12_Input;
  //   Column_12_Data[31:0] = Col_12_Data; Column_13 = Col_13_Input; Column_13_Data[31:0] = Col_13_Data;
  //   Column_14 = Col_14_Input; Column_14_Data[31:0] = Col_14_Data; Column_15 = Col_15_Input;
  //   Column_15_Data[31:0] = Col_15_Data; Column_16 = Col_16_Input; Column_16_Data[31:0] = Col_16_Data;
  //   Column_17 = Col_17_Input; Column_17_Data[31:0] = Col_17_Data; Column_18 = Col_18_Input;
  //   Column_18_Data[31:0] = Col_18_Data; Column_19 = Col_19_Input; Column_19_Data[31:0] = Col_19_Data;
  //   Column_20 = Col_20_Input; Column_20_Data[31:0] = Col_20_Data; Column_21 = Col_21_Input;
  //   Column_21_Data[31:0] = Col_21_Data; Column_22 = Col_22_Input; Column_22_Data[31:0] = Col_22_Data;
  //   Column_23 = Col_23_Input; Column_23_Data[31:0] = Col_23_Data; Column_24 = Col_24_Input;
  //   Column_24_Data[31:0] = Col_24_Data; Column_25 = Col_25_Input; Column_25_Data[31:0] = Col_25_Data;
  //   Column_26 = Col_26_Input; Column_26_Data[31:0] = Col_26_Data; Column_27 = Col_27_Input;
  //   Column_27_Data[31:0] = Col_27_Data; Column_28 = Col_28_Input; Column_28_Data[31:0] = Col_28_Data;
  //   Column_29 = Col_29_Input; Column_29_Data[31:0] = Col_29_Data; Column_30 = Col_30_Input;
  //   Column_30_Data[31:0] = Col_30_Data; Column_31 = Col_31_Input; Column_31_Data[31:0] = Col_31_Data;
  //   Column_32 = Col_32_Input; Column_32_Data[31:0] = Col_32_Data; data[31:0] = Data_Input
endmodule
