// Logisim project logism-img-64x64vfinal.circ as structural Verilog: 3 circuits, main circuit main
module main (
);

  wire clock, Column_1, Column_2, Column_3, Column_4, Column_5, Column_6, Column_7, Column_8, Column_9,
       Column_10, Column_11, Column_12, Column_13, Column_14, Column_15, Column_16, Column_17, Column_18,
       Column_19, Column_20, Column_21, Column_22, Column_23, Column_24, Column_25, Column_26, Column_27,
       Column_28, Column_29, Column_30, Column_31, Column_32;
  wire [4:0] bitselector_1_out;
  wire [11:0] CurrAddress;
  wire [31:0] Column_1_2_Data, Column_1_3_Data, Column_1_Data, Column_2_2_Data, Column_2_3_Data,
       Column_2_Data, Column_3_2_Data, Column_3_3_Data, Column_3_Data, Column_4_2_Data, Column_4_3_Data,
       Column_4_Data, Column_5_2_Data, Column_5_3_Data, Column_5_Data, Column_6_2_Data, Column_6_3_Data,
       Column_6_Data, Column_7_2_Data, Column_7_3_Data, Column_7_Data, Column_8_2_Data, Column_8_3_Data,
       Column_8_Data, Column_9_2_Data, Column_9_3_Data, Column_9_Data, Column_10_2_Data, Column_10_3_Data,
       Column_10_Data, Column_11_2_Data, Column_11_3_Data, Column_11_Data, Column_12_2_Data,
       Column_12_3_Data, Column_12_Data, Column_13_2_Data, Column_13_3_Data, Column_13_Data,
       Column_14_2_Data, Column_14_3_Data, Column_14_Data, Column_15_2_Data, Column_15_3_Data,
       Column_15_Data, Column_16_2_Data, Column_16_3_Data, Column_16_Data, Column_17_2_Data,
       Column_17_3_Data, Column_17_Data, Column_18_2_Data, Column_18_3_Data, Column_18_Data,
       Column_19_2_Data, Column_19_3_Data, Column_19_Data, Column_20_2_Data, Column_20_3_Data,
       Column_20_Data, Column_21_2_Data, Column_21_3_Data, Column_21_Data, Column_22_2_Data,
       Column_22_3_Data, Column_22_Data, Column_23_2_Data, Column_23_3_Data, Column_23_Data,
       Column_24_2_Data, Column_24_3_Data, Column_24_Data, Column_25_2_Data, Column_25_3_Data,
       Column_25_Data, Column_26_2_Data, Column_26_3_Data, Column_26_Data, Column_27_2_Data,
       Column_27_3_Data, Column_27_Data, Column_28_2_Data, Column_28_3_Data, Column_28_Data,
       Column_29_2_Data, Column_29_3_Data, Column_29_Data, Column_30_2_Data, Column_30_3_Data,
       Column_30_Data, Column_31_2_Data, Column_31_3_Data, Column_31_Data, Column_32_2_Data,
       Column_32_3_Data, Column_32_Data, data, data_2, data_3, data_4, Row_1D, Row_2D, Row_3D, Row_4D,
       Row_5D, Row_6D, Row_7D, Row_8D, Row_9D, Row_10D, Row_11D, Row_12D, Row_13D, Row_14D, Row_15D, Row_16D,
       Row_17D, Row_18D, Row_19D, Row_20D, Row_21D, Row_22D, Row_23D, Row_24D, Row_25D, Row_26D, Row_27D,
       Row_28D, Row_29D, Row_30D, Row_31D, Row_32D;

  Counter #(.width(12), .max('hfff)) counter_1 (.Q(CurrAddress), .clk(clock));  // open: load, D, count, carry, clr
  Clock clock_1 (.out(clock));
  RAM #(.addrWidth(12), .dataWidth(32)) ram_1 (.addr(CurrAddress), .data(data));  // open: sel, clk, ld, clr
  RAM #(.addrWidth(12), .dataWidth(32)) ram_2 (.addr(CurrAddress), .data(data_2));  // open: sel, clk, ld, clr
  RAM #(.addrWidth(12), .dataWidth(32)) ram_3 (.addr(CurrAddress), .data(data_3));  // open: sel, clk, ld, clr
  RAM #(.addrWidth(12), .dataWidth(32)) ram_4 (.addr(CurrAddress), .data(data_4));  // open: sel, clk, ld, clr
  Demultiplexer #(.select(5)) demultiplexer_1 (
    .out0(Column_1), .out1(Column_2), .out2(Column_3), .out3(Column_4), .out4(Column_5), .out5(Column_6),
    .out6(Column_7), .out7(Column_8), .out8(Column_9), .out9(Column_10), .out10(Column_11),
    .out11(Column_12), .out12(Column_13), .out13(Column_14), .out14(Column_15), .out15(Column_16),
    .out16(Column_17), .out17(Column_18), .out18(Column_19), .out19(Column_20), .out20(Column_21),
    .out21(Column_22), .out22(Column_23), .out23(Column_24), .out24(Column_25), .out25(Column_26),
    .out26(Column_27), .out27(Column_28), .out28(Column_29), .out29(Column_30), .out30(Column_31),
    .out31(Column_32), .in(1'b1), .sel(bitselector_1_out));  // open: en
  BitSelector #(.width(12), .group(5)) bitselector_1 (.in(CurrAddress), .out(bitselector_1_out), .sel(2'b00));
  Data_Registers_32 data_registers_32_1 (
    .Col_1_Data(Column_1_Data), .Col_2_Data(Column_2_Data), .Col_3_Data(Column_3_Data),
    .Col_4_Data(Column_4_Data), .Col_5_Data(Column_5_Data), .Col_6_Data(Column_6_Data),
    .Col_7_Data(Column_7_Data), .Col_8_Data(Column_8_Data), .Col_9_Data(Column_9_Data),
    .Col_10_Data(Column_10_Data), .Col_11_Data(Column_11_Data), .Col_12_Data(Column_12_Data),
    .Col_13_Data(Column_13_Data), .Col_14_Data(Column_14_Data), .Col_15_Data(Column_15_Data),
    .Col_16_Data(Column_16_Data), .Col_17_Data(Column_17_Data), .Col_18_Data(Column_18_Data),
    .Col_19_Data(Column_19_Data), .Col_20_Data(Column_20_Data), .Col_21_Data(Column_21_Data),
    .Col_22_Data(Column_22_Data), .Col_23_Data(Column_23_Data), .Col_24_Data(Column_24_Data),
    .Col_25_Data(Column_25_Data), .Col_26_Data(Column_26_Data), .Col_27_Data(Column_27_Data),
    .Col_28_Data(Column_28_Data), .Col_29_Data(Column_29_Data), .Col_30_Data(Column_30_Data),
    .Col_31_Data(Column_31_Data), .Col_32_Data(Column_32_Data), .Data_Input(data_3), .Col_1_Input(Column_1),
    .Col_2_Input(Column_2), .Col_3_Input(Column_3), .Col_4_Input(Column_4), .Col_5_Input(Column_5),
    .Col_6_Input(Column_6), .Col_7_Input(Column_7), .Col_8_Input(Column_8), .Col_9_Input(Column_9),
    .Col_10_Input(Column_10), .Col_11_Input(Column_11), .Col_12_Input(Column_12), .Col_13_Input(Column_13),
    .Col_14_Input(Column_14), .Col_15_Input(Column_15), .Col_16_Input(Column_16), .Col_17_Input(Column_17),
    .Col_18_Input(Column_18), .Col_19_Input(Column_19), .Col_20_Input(Column_20), .Col_21_Input(Column_21),
    .Col_22_Input(Column_22), .Col_23_Input(Column_23), .Col_24_Input(Column_24), .Col_25_Input(Column_25),
    .Col_26_Input(Column_26), .Col_27_Input(Column_27), .Col_28_Input(Column_28), .Col_29_Input(Column_29),
    .Col_30_Input(Column_30), .Col_31_Input(Column_31), .Col_32_Input(Column_32));
  Data_Registers_32 data_registers_32_2 (
    .Col_1_Data(Column_1_2_Data), .Col_2_Data(Column_2_2_Data), .Col_3_Data(Column_3_2_Data),
    .Col_4_Data(Column_4_2_Data), .Col_5_Data(Column_5_2_Data), .Col_6_Data(Column_6_2_Data),
    .Col_7_Data(Column_7_2_Data), .Col_8_Data(Column_8_2_Data), .Col_9_Data(Column_9_2_Data),
    .Col_10_Data(Column_10_2_Data), .Col_11_Data(Column_11_2_Data), .Col_12_Data(Column_12_2_Data),
    .Col_13_Data(Column_13_2_Data), .Col_14_Data(Column_14_2_Data), .Col_15_Data(Column_15_2_Data),
    .Col_16_Data(Column_16_2_Data), .Col_17_Data(Column_17_2_Data), .Col_18_Data(Column_18_2_Data),
    .Col_19_Data(Column_19_2_Data), .Col_20_Data(Column_20_2_Data), .Col_21_Data(Column_21_2_Data),
    .Col_22_Data(Column_22_2_Data), .Col_23_Data(Column_23_2_Data), .Col_24_Data(Column_24_2_Data),
    .Col_25_Data(Column_25_2_Data), .Col_26_Data(Column_26_2_Data), .Col_27_Data(Column_27_2_Data),
    .Col_28_Data(Column_28_2_Data), .Col_29_Data(Column_29_2_Data), .Col_30_Data(Column_30_2_Data),
    .Col_31_Data(Column_31_2_Data), .Col_32_Data(Column_32_2_Data), .Data_Input(data_4),
    .Col_1_Input(Column_1), .Col_2_Input(Column_2), .Col_3_Input(Column_3), .Col_4_Input(Column_4),
    .Col_5_Input(Column_5), .Col_6_Input(Column_6), .Col_7_Input(Column_7), .Col_8_Input(Column_8),
    .Col_9_Input(Column_9), .Col_10_Input(Column_10), .Col_11_Input(Column_11), .Col_12_Input(Column_12),
    .Col_13_Input(Column_13), .Col_14_Input(Column_14), .Col_15_Input(Column_15), .Col_16_Input(Column_16),
    .Col_17_Input(Column_17), .Col_18_Input(Column_18), .Col_19_Input(Column_19), .Col_20_Input(Column_20),
    .Col_21_Input(Column_21), .Col_22_Input(Column_22), .Col_23_Input(Column_23), .Col_24_Input(Column_24),
    .Col_25_Input(Column_25), .Col_26_Input(Column_26), .Col_27_Input(Column_27), .Col_28_Input(Column_28),
    .Col_29_Input(Column_29), .Col_30_Input(Column_30), .Col_31_Input(Column_31), .Col_32_Input(Column_32));
  DotMatrix #(.inputtype("row"), .matrixcols(32), .matrixrows(32)) dotmatrix_1 (
    .row0(Row_1D), .row1(Row_2D), .row2(Row_3D), .row3(Row_4D), .row4(Row_5D), .row5(Row_6D), .row6(Row_7D),
    .row7(Row_8D), .row8(Row_9D), .row9(Row_10D), .row10(Row_11D), .row11(Row_12D), .row12(Row_13D),
    .row13(Row_14D), .row14(Row_15D), .row15(Row_16D), .row16(Row_17D), .row17(Row_18D), .row18(Row_19D),
    .row19(Row_20D), .row20(Row_21D), .row21(Row_22D), .row22(Row_23D), .row23(Row_24D), .row24(Row_25D),
    .row25(Row_26D), .row26(Row_27D), .row27(Row_28D), .row28(Row_29D), .row29(Row_30D), .row30(Row_31D),
    .row31(Row_32D));
  DotMatrix #(.matrixcols(32), .matrixrows(32)) dotmatrix_2 (
    .col0(Column_1_Data), .col1(Column_2_Data), .col2(Column_3_Data), .col3(Column_4_Data),
    .col4(Column_5_Data), .col5(Column_6_Data), .col6(Column_7_Data), .col7(Column_8_Data),
    .col8(Column_9_Data), .col9(Column_10_Data), .col10(Column_11_Data), .col11(Column_12_Data),
    .col12(Column_13_Data), .col13(Column_14_Data), .col14(Column_15_Data), .col15(Column_16_Data),
    .col16(Column_17_Data), .col17(Column_18_Data), .col18(Column_19_Data), .col19(Column_20_Data),
    .col20(Column_21_Data), .col21(Column_22_Data), .col22(Column_23_Data), .col23(Column_24_Data),
    .col24(Column_25_Data), .col25(Column_26_Data), .col26(Column_27_Data), .col27(Column_28_Data),
    .col28(Column_29_Data), .col29(Column_30_Data), .col30(Column_31_Data), .col31(Column_32_Data));
  DotMatrix #(.matrixcols(32), .matrixrows(32)) dotmatrix_3 (
    .col0(Column_1_3_Data), .col1(Column_2_3_Data), .col2(Column_3_3_Data), .col3(Column_4_3_Data),
    .col4(Column_5_3_Data), .col5(Column_6_3_Data), .col6(Column_7_3_Data), .col7(Column_8_3_Data),
    .col8(Column_9_3_Data), .col9(Column_10_3_Data), .col10(Column_11_3_Data), .col11(Column_12_3_Data),
    .col12(Column_13_3_Data), .col13(Column_14_3_Data), .col14(Column_15_3_Data), .col15(Column_16_3_Data),
    .col16(Column_17_3_Data), .col17(Column_18_3_Data), .col18(Column_19_3_Data), .col19(Column_20_3_Data),
    .col20(Column_21_3_Data), .col21(Column_22_3_Data), .col22(Column_23_3_Data), .col23(Column_24_3_Data),
    .col24(Column_25_3_Data), .col25(Column_26_3_Data), .col26(Column_27_3_Data), .col27(Column_28_3_Data),
    .col28(Column_29_3_Data), .col29(Column_30_3_Data), .col30(Column_31_3_Data), .col31(Column_32_3_Data));
  DotMatrix #(.matrixcols(32), .matrixrows(32)) dotmatrix_4 (
    .col0(Column_1_2_Data), .col1(Column_2_2_Data), .col2(Column_3_2_Data), .col3(Column_4_2_Data),
    .col4(Column_5_2_Data), .col5(Column_6_2_Data), .col6(Column_7_2_Data), .col7(Column_8_2_Data),
    .col8(Column_9_2_Data), .col9(Column_10_2_Data), .col10(Column_11_2_Data), .col11(Column_12_2_Data),
    .col12(Column_13_2_Data), .col13(Column_14_2_Data), .col14(Column_15_2_Data), .col15(Column_16_2_Data),
    .col16(Column_17_2_Data), .col17(Column_18_2_Data), .col18(Column_19_2_Data), .col19(Column_20_2_Data),
    .col20(Column_21_2_Data), .col21(Column_22_2_Data), .col22(Column_23_2_Data), .col23(Column_24_2_Data),
    .col24(Column_25_2_Data), .col25(Column_26_2_Data), .col26(Column_27_2_Data), .col27(Column_28_2_Data),
    .col28(Column_29_2_Data), .col29(Column_30_2_Data), .col30(Column_31_2_Data), .col31(Column_32_2_Data));
  Data_Registers_32 data_registers_32_3 (
    .Col_1_Data(Column_1_3_Data), .Col_2_Data(Column_2_3_Data), .Col_3_Data(Column_3_3_Data),
    .Col_4_Data(Column_4_3_Data), .Col_5_Data(Column_5_3_Data), .Col_6_Data(Column_6_3_Data),
    .Col_7_Data(Column_7_3_Data), .Col_8_Data(Column_8_3_Data), .Col_9_Data(Column_9_3_Data),
    .Col_10_Data(Column_10_3_Data), .Col_11_Data(Column_11_3_Data), .Col_12_Data(Column_12_3_Data),
    .Col_13_Data(Column_13_3_Data), .Col_14_Data(Column_14_3_Data), .Col_15_Data(Column_15_3_Data),
    .Col_16_Data(Column_16_3_Data), .Col_17_Data(Column_17_3_Data), .Col_18_Data(Column_18_3_Data),
    .Col_19_Data(Column_19_3_Data), .Col_20_Data(Column_20_3_Data), .Col_21_Data(Column_21_3_Data),
    .Col_22_Data(Column_22_3_Data), .Col_23_Data(Column_23_3_Data), .Col_24_Data(Column_24_3_Data),
    .Col_25_Data(Column_25_3_Data), .Col_26_Data(Column_26_3_Data), .Col_27_Data(Column_27_3_Data),
    .Col_28_Data(Column_28_3_Data), .Col_29_Data(Column_29_3_Data), .Col_30_Data(Column_30_3_Data),
    .Col_31_Data(Column_31_3_Data), .Col_32_Data(Column_32_3_Data), .Data_Input(data_2),
    .Col_1_Input(Column_1), .Col_2_Input(Column_2), .Col_3_Input(Column_3), .Col_4_Input(Column_4),
    .Col_5_Input(Column_5), .Col_6_Input(Column_6), .Col_7_Input(Column_7), .Col_8_Input(Column_8),
    .Col_9_Input(Column_9), .Col_10_Input(Column_10), .Col_11_Input(Column_11), .Col_12_Input(Column_12),
    .Col_13_Input(Column_13), .Col_14_Input(Column_14), .Col_15_Input(Column_15), .Col_16_Input(Column_16),
    .Col_17_Input(Column_17), .Col_18_Input(Column_18), .Col_19_Input(Column_19), .Col_20_Input(Column_20),
    .Col_21_Input(Column_21), .Col_22_Input(Column_22), .Col_23_Input(Column_23), .Col_24_Input(Column_24),
    .Col_25_Input(Column_25), .Col_26_Input(Column_26), .Col_27_Input(Column_27), .Col_28_Input(Column_28),
    .Col_29_Input(Column_29), .Col_30_Input(Column_30), .Col_31_Input(Column_31), .Col_32_Input(Column_32));
  Data_Registers_32 data_registers_32_4 (
    .Col_1_Data(Row_1D), .Col_2_Data(Row_2D), .Col_3_Data(Row_3D), .Col_4_Data(Row_4D), .Col_5_Data(Row_5D),
    .Col_6_Data(Row_6D), .Col_7_Data(Row_7D), .Col_8_Data(Row_8D), .Col_9_Data(Row_9D),
    .Col_10_Data(Row_10D), .Col_11_Data(Row_11D), .Col_12_Data(Row_12D), .Col_13_Data(Row_13D),
    .Col_14_Data(Row_14D), .Col_15_Data(Row_15D), .Col_16_Data(Row_16D), .Col_17_Data(Row_17D),
    .Col_18_Data(Row_18D), .Col_19_Data(Row_19D), .Col_20_Data(Row_20D), .Col_21_Data(Row_21D),
    .Col_22_Data(Row_22D), .Col_23_Data(Row_23D), .Col_24_Data(Row_24D), .Col_25_Data(Row_25D),
    .Col_26_Data(Row_26D), .Col_27_Data(Row_27D), .Col_28_Data(Row_28D), .Col_29_Data(Row_29D),
    .Col_30_Data(Row_30D), .Col_31_Data(Row_31D), .Col_32_Data(Row_32D), .Data_Input(data),
    .Col_1_Input(Column_1), .Col_2_Input(Column_2), .Col_3_Input(Column_3), .Col_4_Input(Column_4),
    .Col_5_Input(Column_5), .Col_6_Input(Column_6), .Col_7_Input(Column_7), .Col_8_Input(Column_8),
    .Col_9_Input(Column_9), .Col_10_Input(Column_10), .Col_11_Input(Column_11), .Col_12_Input(Column_12),
    .Col_13_Input(Column_13), .Col_14_Input(Column_14), .Col_15_Input(Column_15), .Col_16_Input(Column_16),
    .Col_17_Input(Column_17), .Col_18_Input(Column_18), .Col_19_Input(Column_19), .Col_20_Input(Column_20),
    .Col_21_Input(Column_21), .Col_22_Input(Column_22), .Col_23_Input(Column_23), .Col_24_Input(Column_24),
    .Col_25_Input(Column_25), .Col_26_Input(Column_26), .Col_27_Input(Column_27), .Col_28_Input(Column_28),
    .Col_29_Input(Column_29), .Col_30_Input(Column_30), .Col_31_Input(Column_31), .Col_32_Input(Column_32));

  // Notes on the sheet:
  //   Data 1 RAM
  //   Data 2 RAM
  //   Data 3 RAM
  //   Data 4 RAM
endmodule

module Data_Registers_4 (
  input  Column_1_Input,
  input  Column_2_Input,
  input  Column_3_Input,
  input  Column_4_Input,
  input  [31:0] Data,
  output [31:0] out_6,
  output [31:0] out_7,
  output [31:0] out_8,
  output [31:0] out_9
);

  Register #(.width(32), .trigger("high")) register_1 (.D(Data), .Q(out_6), .clk(Column_1_Input));  // open: en, clr
  Register #(.width(32), .trigger("high")) register_2 (.D(Data), .Q(out_7), .clk(Column_2_Input));  // open: en, clr
  Register #(.width(32), .trigger("high")) register_3 (.D(Data), .Q(out_8), .clk(Column_3_Input));  // open: en, clr
  Register #(.width(32), .trigger("high")) register_4 (.D(Data), .Q(out_9), .clk(Column_4_Input));  // open: en, clr

  // Other names for the same wires on the sheet: Column_1 = Column_1_Input; Column_1_Data[31:0] = out_6;
  //   Column_2 = Column_2_Input; Column_2_Data[31:0] = out_7; Column_3 = Column_3_Input; Column_3_Data[31:0] = out_8;
  //   Column_4 = Column_4_Input; Column_4_Data[31:0] = out_9
endmodule

module Data_Registers_32 (
  input  Col_1_Input,
  input  Col_2_Input,
  input  Col_3_Input,
  input  Col_4_Input,
  input  Col_5_Input,
  input  Col_6_Input,
  input  Col_7_Input,
  input  Col_8_Input,
  input  Col_9_Input,
  input  Col_10_Input,
  input  Col_11_Input,
  input  Col_12_Input,
  input  Col_13_Input,
  input  Col_14_Input,
  input  Col_15_Input,
  input  Col_16_Input,
  input  Col_17_Input,
  input  Col_18_Input,
  input  Col_19_Input,
  input  Col_20_Input,
  input  Col_21_Input,
  input  Col_22_Input,
  input  Col_23_Input,
  input  Col_24_Input,
  input  Col_25_Input,
  input  Col_26_Input,
  input  Col_27_Input,
  input  Col_28_Input,
  input  Col_29_Input,
  input  Col_30_Input,
  input  [31:0] Data_Input,
  input  Col_31_Input,
  input  Col_32_Input,
  output [31:0] Col_1_Data,
  output [31:0] Col_2_Data,
  output [31:0] Col_3_Data,
  output [31:0] Col_4_Data,
  output [31:0] Col_5_Data,
  output [31:0] Col_6_Data,
  output [31:0] Col_7_Data,
  output [31:0] Col_8_Data,
  output [31:0] Col_9_Data,
  output [31:0] Col_10_Data,
  output [31:0] Col_11_Data,
  output [31:0] Col_12_Data,
  output [31:0] Col_13_Data,
  output [31:0] Col_14_Data,
  output [31:0] Col_15_Data,
  output [31:0] Col_16_Data,
  output [31:0] Col_17_Data,
  output [31:0] Col_18_Data,
  output [31:0] Col_19_Data,
  output [31:0] Col_20_Data,
  output [31:0] Col_21_Data,
  output [31:0] Col_22_Data,
  output [31:0] Col_23_Data,
  output [31:0] Col_24_Data,
  output [31:0] Col_25_Data,
  output [31:0] Col_26_Data,
  output [31:0] Col_27_Data,
  output [31:0] Col_28_Data,
  output [31:0] Col_29_Data,
  output [31:0] Col_30_Data,
  output [31:0] Col_31_Data,
  output [31:0] Col_32_Data
);

  Data_Registers_4 _1_4 (
    .out_6(Col_1_Data), .out_7(Col_2_Data), .out_8(Col_3_Data), .out_9(Col_4_Data), .Data(Data_Input),
    .Column_1_Input(Col_1_Input), .Column_2_Input(Col_2_Input), .Column_3_Input(Col_3_Input),
    .Column_4_Input(Col_4_Input));
  Data_Registers_4 _1_4_2 (
    .out_6(Col_9_Data), .out_7(Col_10_Data), .out_8(Col_11_Data), .out_9(Col_12_Data), .Data(Data_Input),
    .Column_1_Input(Col_9_Input), .Column_2_Input(Col_10_Input), .Column_3_Input(Col_11_Input),
    .Column_4_Input(Col_12_Input));
  Data_Registers_4 _1_4_3 (
    .out_6(Col_17_Data), .out_7(Col_18_Data), .out_8(Col_19_Data), .out_9(Col_20_Data), .Data(Data_Input),
    .Column_1_Input(Col_17_Input), .Column_2_Input(Col_18_Input), .Column_3_Input(Col_19_Input),
    .Column_4_Input(Col_20_Input));
  Data_Registers_4 _1_4_4 (
    .out_6(Col_25_Data), .out_7(Col_26_Data), .out_8(Col_27_Data), .out_9(Col_28_Data), .Data(Data_Input),
    .Column_1_Input(Col_25_Input), .Column_2_Input(Col_26_Input), .Column_3_Input(Col_27_Input),
    .Column_4_Input(Col_28_Input));
  Data_Registers_4 _5_8 (
    .out_6(Col_5_Data), .out_7(Col_6_Data), .out_8(Col_7_Data), .out_9(Col_8_Data), .Data(Data_Input),
    .Column_1_Input(Col_5_Input), .Column_2_Input(Col_6_Input), .Column_3_Input(Col_7_Input),
    .Column_4_Input(Col_8_Input));
  Data_Registers_4 _1_4_5 (
    .out_6(Col_13_Data), .out_7(Col_14_Data), .out_8(Col_15_Data), .out_9(Col_16_Data), .Data(Data_Input),
    .Column_1_Input(Col_13_Input), .Column_2_Input(Col_14_Input), .Column_3_Input(Col_15_Input),
    .Column_4_Input(Col_16_Input));
  Data_Registers_4 _1_4_6 (
    .out_6(Col_21_Data), .out_7(Col_22_Data), .out_8(Col_23_Data), .out_9(Col_24_Data), .Data(Data_Input),
    .Column_1_Input(Col_21_Input), .Column_2_Input(Col_22_Input), .Column_3_Input(Col_23_Input),
    .Column_4_Input(Col_24_Input));
  Data_Registers_4 _1_4_7 (
    .out_6(Col_29_Data), .out_7(Col_30_Data), .out_8(Col_31_Data), .out_9(Col_32_Data), .Data(Data_Input),
    .Column_1_Input(Col_29_Input), .Column_2_Input(Col_30_Input), .Column_3_Input(Col_31_Input),
    .Column_4_Input(Col_32_Input));

  // Other names for the same wires on the sheet: Column_1 = Col_1_Input; Column_1_Data[31:0] = Col_1_Data;
  //   Column_2 = Col_2_Input; Column_2_Data[31:0] = Col_2_Data; Column_3 = Col_3_Input;
  //   Column_3_Data[31:0] = Col_3_Data; Column_4 = Col_4_Input; Column_4_Data[31:0] = Col_4_Data;
  //   Column_5 = Col_5_Input; Column_5_Data[31:0] = Col_5_Data; Column_6 = Col_6_Input;
  //   Column_6_Data[31:0] = Col_6_Data; Column_7 = Col_7_Input; Column_7_Data[31:0] = Col_7_Data;
  //   Column_8 = Col_8_Input; Column_8_Data[31:0] = Col_8_Data; Column_9 = Col_9_Input;
  //   Column_9_Data[31:0] = Col_9_Data; Column_10 = Col_10_Input; Column_10_Data[31:0] = Col_10_Data;
  //   Column_11 = Col_11_Input; Column_11_Data[31:0] = Col_11_Data; Column_12 = Col_12_Input;
  //   Column_12_Data[31:0] = Col_12_Data; Column_13 = Col_13_Input; Column_13_Data[31:0] = Col_13_Data;
  //   Column_14 = Col_14_Input; Column_14_Data[31:0] = Col_14_Data; Column_15 = Col_15_Input;
  //   Column_15_Data[31:0] = Col_15_Data; Column_16 = Col_16_Input; Column_16_Data[31:0] = Col_16_Data;
  //   Column_17 = Col_17_Input; Column_17_Data[31:0] = Col_17_Data; Column_18 = Col_18_Input;
  //   Column_18_Data[31:0] = Col_18_Data; Column_19 = Col_19_Input; Column_19_Data[31:0] = Col_19_Data;
  //   Column_20 = Col_20_Input; Column_20_Data[31:0] = Col_20_Data; Column_21 = Col_21_Input;
  //   Column_21_Data[31:0] = Col_21_Data; Column_22 = Col_22_Input; Column_22_Data[31:0] = Col_22_Data;
  //   Column_23 = Col_23_Input; Column_23_Data[31:0] = Col_23_Data; Column_24 = Col_24_Input;
  //   Column_24_Data[31:0] = Col_24_Data; Column_25 = Col_25_Input; Column_25_Data[31:0] = Col_25_Data;
  //   Column_26 = Col_26_Input; Column_26_Data[31:0] = Col_26_Data; Column_27 = Col_27_Input;
  //   Column_27_Data[31:0] = Col_27_Data; Column_28 = Col_28_Input; Column_28_Data[31:0] = Col_28_Data;
  //   Column_29 = Col_29_Input; Column_29_Data[31:0] = Col_29_Data; Column_30 = Col_30_Input;
  //   Column_30_Data[31:0] = Col_30_Data; Column_31 = Col_31_Input; Column_31_Data[31:0] = Col_31_Data;
  //   Column_32 = Col_32_Input; Column_32_Data[31:0] = Col_32_Data; data[31:0] = Data_Input
endmodule
